# Fritzing sketch rgblamp (saved by Fritzing 0.9.6b)
circuit board: 7cm x 5cm
breadboards: 1

parts:
  NANO = Arduino Nano (Rev3.0)
  POWER = female pin header, 4 pins [form="♀ (female)"]
  FUSE = Resettable Fuse PTC [package=ptc]
  C1 = Electrolytic Capacitor [capacitance=1µF voltage=35V package="100 mil [THT, electrolytic]"]
  1k = Resistor [tolerance=±5% power=0.25 resistance=1k package=THT]
  1k_2 = Resistor [tolerance=±5% power=0.25 resistance=1k package=THT]
  1k_3 = Resistor [tolerance=±5% power=0.25 resistance=1k package=THT]
  Encoder = female pin header, 4 pins [form="♀ (female)"]
  LEDSTRIP = female pin header, 3 pins [form="♀ (female)"]
  Extra = female pin header, 7 pins [form="♀ (female)"]
  Extra_2 = female pin header, 8 pins [form="♀ (female)"]
  J1 = female pin header, 1 pin [form="♀ (female)"]

nets:
  N1: NANO.GND, POWER.pin3, POWER.pin4, C1.-, Encoder.pin1, LEDSTRIP.pin2, J1.pin1
  N2: NANO.D2, 1k.Pin_1, Encoder.pin2
  N3: NANO.D3, 1k_2.Pin_1, Encoder.pin3
  N4: NANO.D4, 1k_3.Pin_1, Encoder.pin4
  N5: NANO.D5, LEDSTRIP.pin3
  N6: NANO.D6, Extra.pin1
  N7: NANO.D7, Extra.pin2
  N8: NANO.D8, Extra.pin3
  N9: NANO.D9, Extra.pin4
  N10: NANO.D10, Extra.pin5
  N11: NANO.D11/MOSI, Extra.pin6
  N12: NANO.D12/MISO, Extra.pin7
  N13: NANO.VIN, FUSE.2, C1.+, LEDSTRIP.pin1
  N14: NANO.5V, 1k.Pin_0, 1k_2.Pin_0, 1k_3.Pin_0
  N15: NANO.A7, Extra_2.pin1
  N16: NANO.A6, Extra_2.pin2
  N17: NANO.A5, Extra_2.pin3
  N18: NANO.A4, Extra_2.pin4
  N19: NANO.A3, Extra_2.pin5
  N20: NANO.A2, Extra_2.pin6
  N21: NANO.A1, Extra_2.pin7
  N22: NANO.A0, Extra_2.pin8
  N23: POWER.pin1, POWER.pin2, FUSE.1
